// Logisim project sap-1.circ as structural Verilog
module sap_1 (
  input  [7:0] in_1,
  input  in_2,
  input  in_3,
  input  in_4,
  input  in_5,
  input  in_6,
  input  in_7,
  input  in_8,
  input  in_9,
  input  in_10,
  input  Run_Prog,
  input  A0,
  input  A1,
  input  A2,
  input  A3,
  output [7:0] out_16
);

  wire accumulator_a_1_q0, accumulator_a_1_q1, accumulator_a_1_q2, accumulator_a_1_q3, accumulator_a_1_q4,
       accumulator_a_1_q5, accumulator_a_1_q6, accumulator_a_1_q7, CE_N, CLK, CLK_N, CLR, CLR_N, Cp, Ea,
       Ei_N, Ep, Eu, GEN_out, HLT_N, instruction_decoder_1_add, instruction_decoder_1_lda,
       instruction_decoder_1_out, instruction_decoder_1_sub, intruction_register_1_i4,
       intruction_register_1_i5, intruction_register_1_i6, intruction_register_1_i7, La_N, Lb_N, Li_N, Lm_N,
       Lo_N, memory_address_register_1_q0, memory_address_register_1_q1, memory_address_register_1_q2,
       memory_address_register_1_q3, nibble_multiplexer_1_q0, nibble_multiplexer_1_q1,
       nibble_multiplexer_1_q2, nibble_multiplexer_1_q3, not_1_out, output_register_1_q0,
       output_register_1_q1, output_register_1_q2, output_register_1_q3, output_register_1_q4,
       output_register_1_q5, output_register_1_q6, output_register_1_q7, program_counter_1_q0,
       program_counter_1_q1, program_counter_1_q2, program_counter_1_q3, ram_16x8_1_o4_n, ram_16x8_1_o5_n,
       ram_16x8_1_o6_n, ram_16x8_1_o7_n, register_b_1_q0, register_b_1_q1, register_b_1_q2, register_b_1_q3,
       register_b_1_q4, register_b_1_q5, register_b_1_q6, register_b_1_q7, ring_counter_1_t1,
       ring_counter_1_t2, ring_counter_1_t3, ring_counter_1_t4, ring_counter_1_t5, ring_counter_1_t6,
       START_CLEAR_out, Su;

  Button START_CLEAR (.out(START_CLEAR_out));
  Clock GEN (.out(GEN_out));
  not not_1 (not_1_out, START_CLEAR_out);
  LED led_1 (.in(in_1[5]));
  LED led_2 (.in(in_1[6]));
  LED led_3 (.in(in_1[7]));
  nand nand_1 (CLR_N, START_CLEAR_out, CLR);
  nand nand_2 (CLR, CLR_N, not_1_out);
  LED led_4 (.in(in_1[3]));
  LED led_5 (.in(in_1[2]));
  LED led_6 (.in(in_1[1]));
  LED led_7 (.in(in_1[4]));
  clock clock_1 (.HLT_N(HLT_N), .CLK(CLK), .CLK_N(CLK_N), .GEN(GEN_out));
  memory_address_register memory_address_register_1 (
    .Lm_N(Lm_N), .CLK(CLK), .D0(program_counter_1_q0), .D1(program_counter_1_q1), .D2(program_counter_1_q2),
    .D3(program_counter_1_q3), .Q0(memory_address_register_1_q0), .Q1(memory_address_register_1_q1),
    .Q2(memory_address_register_1_q2), .Q3(memory_address_register_1_q3));
  LED led_8 (.in(in_1[0]));
  // Probe on nothing
  nibble_multiplexer nibble_multiplexer_1 (
    .S(Run_Prog), .A0(memory_address_register_1_q0), .A1(memory_address_register_1_q1),
    .Q0(nibble_multiplexer_1_q0), .A2(memory_address_register_1_q2), .A3(memory_address_register_1_q3),
    .B0(A0), .B1(A1), .B2(A2), .B3(A3), .Q1(nibble_multiplexer_1_q1), .Q2(nibble_multiplexer_1_q2),
    .Q3(nibble_multiplexer_1_q3));
  program_counter_program_counter program_counter_1 (
    .Cp(Cp), .CLK_N(CLK_N), .CLR_N(CLR_N), .Ep(Ep), .Q0(program_counter_1_q0), .Q1(program_counter_1_q1),
    .Q2(program_counter_1_q2), .Q3(program_counter_1_q3));
  RAM_16x8 ram_16x8_1 (
    .D0(in_3), .D1(in_4), .D2(in_5), .D3(in_6), .D4(in_7), .D5(in_8), .D6(in_9), .D7(in_10),
    .A0(nibble_multiplexer_1_q0), .A1(nibble_multiplexer_1_q1), .A2(nibble_multiplexer_1_q2),
    .A3(nibble_multiplexer_1_q3), .WE_N(in_2), .CE_N(CE_N), .O0_N(program_counter_1_q0),
    .O1_N(program_counter_1_q1), .O2_N(program_counter_1_q2), .O3_N(program_counter_1_q3),
    .O4_N(ram_16x8_1_o4_n), .O5_N(ram_16x8_1_o5_n), .O6_N(ram_16x8_1_o6_n), .O7_N(ram_16x8_1_o7_n));
  // Probe on ram_16x8_1_o7_n
  // Probe on ram_16x8_1_o6_n
  // Probe on ram_16x8_1_o5_n
  // Probe on program_counter_1_q3
  // Probe on program_counter_1_q2
  // Probe on program_counter_1_q1
  // Probe on ram_16x8_1_o4_n
  // Probe on program_counter_1_q0
  accumulator_a accumulator_a_1 (
    .Ea(Ea), .La_N(La_N), .CLK(CLK), .D0(program_counter_1_q0), .D1(program_counter_1_q1),
    .D2(program_counter_1_q2), .D3(program_counter_1_q3), .D4(ram_16x8_1_o4_n), .D5(ram_16x8_1_o5_n),
    .D6(ram_16x8_1_o6_n), .D7(ram_16x8_1_o7_n), .Q0_Z(program_counter_1_q0), .Q1_Z(program_counter_1_q1),
    .Q2_Z(program_counter_1_q2), .Q3_Z(program_counter_1_q3), .Q0(accumulator_a_1_q0),
    .Q1(accumulator_a_1_q1), .Q2(accumulator_a_1_q2), .Q3(accumulator_a_1_q3), .Q4_Z(ram_16x8_1_o4_n),
    .Q5_Z(ram_16x8_1_o5_n), .Q6_Z(ram_16x8_1_o6_n), .Q7_Z(ram_16x8_1_o7_n), .Q4(accumulator_a_1_q4),
    .Q5(accumulator_a_1_q5), .Q6(accumulator_a_1_q6), .Q7(accumulator_a_1_q7));
  register_b_register_b register_b_1 (
    .La_N(Lb_N), .CLK(CLK), .D0(program_counter_1_q0), .D1(program_counter_1_q1), .D2(program_counter_1_q2),
    .D3(program_counter_1_q3), .D4(ram_16x8_1_o4_n), .D5(ram_16x8_1_o5_n), .D6(ram_16x8_1_o6_n),
    .D7(ram_16x8_1_o7_n), .Q0(register_b_1_q0), .Q1(register_b_1_q1), .Q2(register_b_1_q2),
    .Q3(register_b_1_q3), .Q4(register_b_1_q4), .Q5(register_b_1_q5), .Q6(register_b_1_q6),
    .Q7(register_b_1_q7));
  LED L7 (.in(output_register_1_q7));
  output_register_output_register output_register_1 (
    .CLK(CLK), .D0(program_counter_1_q0), .D1(program_counter_1_q1), .D2(program_counter_1_q2),
    .D3(program_counter_1_q3), .D4(ram_16x8_1_o4_n), .D5(ram_16x8_1_o5_n), .D6(ram_16x8_1_o6_n),
    .D7(ram_16x8_1_o7_n), .Q0(output_register_1_q0), .Q1(output_register_1_q1), .Q2(output_register_1_q2),
    .Q3(output_register_1_q3), .Q4(output_register_1_q4), .Q5(output_register_1_q5),
    .Q6(output_register_1_q6), .Q7(output_register_1_q7), .Lo_N(Lo_N));
  intruction_register intruction_register_1 (
    .Ei_N(Ei_N), .Li_N(Li_N), .CLK(CLK), .D0(program_counter_1_q0), .D1(program_counter_1_q1),
    .D2(program_counter_1_q2), .D3(program_counter_1_q3), .D4(ram_16x8_1_o4_n), .D5(ram_16x8_1_o5_n),
    .D6(ram_16x8_1_o6_n), .D7(ram_16x8_1_o7_n), .Q0(program_counter_1_q0), .Q1(program_counter_1_q1),
    .Q2(program_counter_1_q2), .Q3(program_counter_1_q3), .I4(intruction_register_1_i4),
    .I5(intruction_register_1_i5), .I6(intruction_register_1_i6), .I7(intruction_register_1_i7), .CLR_N(CLR_N));
  LED L4 (.in(output_register_1_q4));
  LED L5 (.in(output_register_1_q5));
  LED L3 (.in(output_register_1_q3));
  LED L6 (.in(output_register_1_q6));
  LED L2 (.in(output_register_1_q2));
  LED L1 (.in(output_register_1_q1));
  LED L0 (.in(output_register_1_q0));
  adder_substr adder_substr_1 (
    .Eu(Eu), .A7(accumulator_a_1_q7), .A6(accumulator_a_1_q6), .A5(accumulator_a_1_q5),
    .A4(accumulator_a_1_q4), .A3(accumulator_a_1_q3), .A2(accumulator_a_1_q2), .A1(accumulator_a_1_q1),
    .A0(accumulator_a_1_q0), .B7(register_b_1_q7), .B6(register_b_1_q6), .B5(register_b_1_q5),
    .B4(register_b_1_q4), .B3(register_b_1_q3), .B2(register_b_1_q2), .B1(register_b_1_q1),
    .B0(register_b_1_q0), .S0(program_counter_1_q0), .S1(program_counter_1_q1), .S2(program_counter_1_q2),
    .S3(program_counter_1_q3), .S4(ram_16x8_1_o4_n), .S5(ram_16x8_1_o5_n), .S6(ram_16x8_1_o6_n), .Su(Su),
    .S7(ram_16x8_1_o7_n));
  ring_counter ring_counter_1 (
    .CLK(CLK), .CLR_N(CLR_N), .T1(ring_counter_1_t1), .T2(ring_counter_1_t2), .T3(ring_counter_1_t3),
    .T4(ring_counter_1_t4), .T5(ring_counter_1_t5), .T6(ring_counter_1_t6));
  instruction_decoder instruction_decoder_1 (
    .LDA(instruction_decoder_1_lda), .ADD(instruction_decoder_1_add), .SUB(instruction_decoder_1_sub),
    .OUT(instruction_decoder_1_out), .HLT_N(HLT_N), .I7(intruction_register_1_i7),
    .I6(intruction_register_1_i6), .I5(intruction_register_1_i5), .I4(intruction_register_1_i4));
  control_matrix control_matrix_1 (
    .T6(ring_counter_1_t6), .T5(ring_counter_1_t5), .T4(ring_counter_1_t4), .T3(ring_counter_1_t3),
    .T2(ring_counter_1_t2), .T1(ring_counter_1_t1), .LDA(instruction_decoder_1_lda),
    .ADD(instruction_decoder_1_add), .SUB(instruction_decoder_1_sub), .OUT(instruction_decoder_1_out),
    .Cp(Cp), .Ep(Ep), .Lm_N(Lm_N), .CE_N(CE_N), .Li_N(Li_N), .Ei_N(Ei_N), .La_N(La_N), .Ea(Ea), .Su(Su),
    .Eu(Eu), .Lb_N(Lb_N), .Lo_N(Lo_N));
endmodule
